# Fritzing sketch Arduino Due Interface Board 10-terminal (saved by Fritzing 0.9.3b)
circuit board: 8.14cm x 5.08cm
breadboards: 1

parts:
  J1 = screw terminal, 10 pins
  J2 = screw terminal, 10 pins
  74AHCT125 = IC, DIP package, 16 pins [chip_label=IC]

nets:
  N1: J1.pin1, J2.pin10, 74AHCT125.pin1, 74AHCT125.pin4, 74AHCT125.pin7, 74AHCT125.pin12, 74AHCT125.pin15
  N2: J1.pin5, J2.pin6
  N3: J1.pin6, J2.pin5
  N4: J1.pin7, J2.pin4
  N5: J1.pin8, J2.pin3
  N6: J1.pin9, 74AHCT125.pin5
  N7: J2.pin2, 74AHCT125.pin6
